// Logisim project Unit_Convertor.circ as structural Verilog: 1 circuit, main circuit main
module main (
  input  [1:0] in_1,
  input  [10:0] in_2,
  input  in_3,
  input  [1:0] in_4,
  output [15:0] out_5,
  output [15:0] out_6,
  output [15:0] out_7,
  output [15:0] out_8,
  output out_9,
  output out_10,
  output out_11,
  output out_12,
  output Meters,
  output Inch,
  output Foot,
  output Yard,
  output Celsius,
  output Fahrenheite,
  output Kelvin,
  output out_20,
  output Kg,
  output Ounce,
  output Pound,
  output Force,
  output Liter,
  output Gallons,
  output Cups,
  output Pints
);

  wire comparator_1_lt, comparator_2_lt, comparator_3_lt, comparator_4_lt;
  wire [15:0] adder_1_out, adder_2_out, adder_3_out, bit_extender_1_out, demultiplexer_1_out0,
       demultiplexer_1_out1, demultiplexer_1_out2, demultiplexer_1_out3, demultiplexer_2_out0,
       demultiplexer_2_out1, demultiplexer_2_out2, demultiplexer_2_out3, demultiplexer_3_out0,
       demultiplexer_3_out1, demultiplexer_3_out2, demultiplexer_3_out3, demultiplexer_4_out0,
       demultiplexer_4_out1, demultiplexer_4_out2, demultiplexer_4_out3, demultiplexer_5_out0,
       demultiplexer_5_out1, demultiplexer_5_out2, demultiplexer_5_out3, divider_1_out, divider_2_out,
       divider_3_out, divider_4_out, divider_5_out, divider_6_out, divider_7_out, divider_8_out,
       divider_9_out, divider_10_out, divider_11_out, divider_12_out, divider_22_out, divider_23_out,
       input11, input12, input13, input14, input21, input22, input23, input24, input31, input32, input33,
       input34, input41, input42, input43, input44, multiplexer_5_out, multiplexer_6_out, multiplexer_7_out,
       multiplexer_8_out, multiplexer_9_out, multiplexer_10_out, multiplexer_11_out, multiplexer_12_out,
       multiplexer_13_out, multiplexer_14_out, multiplier_1_out, multiplier_2_out, multiplier_3_out,
       multiplier_4_out, multiplier_5_out, multiplier_6_out, multiplier_7_out, multiplier_8_out,
       multiplier_9_out, multiplier_10_out, multiplier_11_out, multiplier_12_out, multiplier_13_out,
       multiplier_14_out, multiplier_15_out, multiplier_16_out, multiplier_17_out, multiplier_18_out,
       multiplier_19_out, multiplier_20_out, multiplier_21_out, negator_1_out, negator_2_out, negator_3_out,
       negator_4_out, negator_5_out, negator_6_out, negator_7_out, negator_8_out, negator_9_out,
       negator_10_out, negator_11_out, negator_12_out, negator_13_out, subtractor_1_out, subtractor_2_out,
       subtractor_3_out;

  Multiplexer #(.select(2), .width(16)) multiplexer_1 (
    .in0(input11), .in1(input21), .in2(input31), .in3(input41), .out(out_5), .sel(in_1));  // open: en
  Decoder #(.select(2)) decoder_1 (.out0(Foot), .out1(Celsius), .out2(Force), .out3(Cups), .sel(in_1));  // open: en
  Multiplexer #(.select(2), .width(16)) multiplexer_2 (
    .in0(input12), .in1(input22), .in2(input32), .in3(input42), .out(out_6), .sel(in_1));  // open: en
  assign bit_extender_1_out = {{5{1'b0}}, in_2};  // Bit_Extender bit_extender_1
  Demultiplexer #(.select(2), .width(16)) demultiplexer_1 (
    .out0(demultiplexer_1_out0), .out1(demultiplexer_1_out1), .out2(demultiplexer_1_out2),
    .out3(demultiplexer_1_out3), .in(bit_extender_1_out), .sel(in_1));  // open: en
  Multiplexer #(.select(2), .width(16)) multiplexer_3 (
    .in0(input13), .in1(input23), .in2(input33), .in3(input43), .out(out_7), .sel(in_1));  // open: en
  Multiplexer #(.select(2), .width(16)) multiplexer_4 (
    .in0(input14), .in1(input24), .in2(input34), .in3(input44), .out(out_8), .sel(in_1));  // open: en
  Negator #(.width(16)) negator_1 (.in(demultiplexer_1_out1), .out(negator_1_out));
  Demultiplexer #(.select(2), .width(16)) demultiplexer_2 (
    .out0(demultiplexer_2_out0), .out1(demultiplexer_2_out1), .out2(demultiplexer_2_out2),
    .out3(demultiplexer_2_out3), .in(demultiplexer_1_out2), .sel(in_4));  // open: en
  Demultiplexer #(.select(2), .width(16)) demultiplexer_3 (
    .out0(demultiplexer_3_out0), .out1(demultiplexer_3_out1), .out2(demultiplexer_3_out2),
    .out3(demultiplexer_3_out3), .in(demultiplexer_1_out3), .sel(in_4));  // open: en
  Demultiplexer #(.select(2), .width(16)) demultiplexer_4 (
    .out0(demultiplexer_4_out0), .out1(demultiplexer_4_out1), .out2(demultiplexer_4_out2),
    .out3(demultiplexer_4_out3), .in(demultiplexer_1_out0), .sel(in_4));  // open: en
  Multiplexer #(.width(16)) multiplexer_5 (
    .in0(demultiplexer_1_out1), .in1(negator_1_out), .out(multiplexer_5_out), .sel(in_3));  // open: en
  Demultiplexer #(.select(2), .width(16)) demultiplexer_5 (
    .out0(demultiplexer_5_out0), .out1(demultiplexer_5_out1), .out2(demultiplexer_5_out2),
    .out3(demultiplexer_5_out3), .in(multiplexer_5_out), .sel(in_4));  // open: en
  Subtractor #(.width(16)) subtractor_1 (
    .a(demultiplexer_5_out1), .b(16'h20), .out(subtractor_1_out));  // open: bin, bout
  Multiplier #(.width(16)) multiplier_1 (.a(subtractor_1_out), .b(16'h37), .out(multiplier_1_out));  // open: cin, cout
  Subtractor #(.width(16)) subtractor_2 (
    .a(demultiplexer_5_out2), .b(16'h111), .out(subtractor_2_out));  // open: bin, bout
  Subtractor #(.width(16)) subtractor_3 (
    .a(demultiplexer_5_out3), .b(16'h1eb), .out(subtractor_3_out));  // open: bin, bout
  Multiplier #(.width(16)) multiplier_2 (
    .a(demultiplexer_2_out1), .b(16'h2d), .out(multiplier_2_out));  // open: cin, cout
  Multiplier #(.width(16)) multiplier_3 (
    .a(demultiplexer_2_out2), .b(16'h3), .out(multiplier_3_out));  // open: cin, cout
  Divider #(.width(16)) divider_1 (.a(demultiplexer_2_out3), .b(16'ha), .out(divider_1_out));  // open: upper, rem
  Multiplier #(.width(16)) multiplier_4 (
    .a(demultiplexer_3_out1), .b(16'h26), .out(multiplier_4_out));  // open: cin, cout
  Multiplier #(.width(16)) multiplier_5 (
    .a(demultiplexer_3_out2), .b(16'h18), .out(multiplier_5_out));  // open: cin, cout
  Multiplier #(.width(16)) multiplier_6 (
    .a(demultiplexer_3_out3), .b(16'h2f), .out(multiplier_6_out));  // open: cin, cout
  Multiplier #(.width(16)) multiplier_7 (
    .a(demultiplexer_4_out1), .b(16'h2), .out(multiplier_7_out));  // open: cin, cout
  Multiplier #(.width(16)) multiplier_8 (
    .a(demultiplexer_4_out2), .b(16'h3), .out(multiplier_8_out));  // open: cin, cout
  Multiplier #(.width(16)) multiplier_9 (
    .a(demultiplexer_4_out3), .b(16'h5b), .out(multiplier_9_out));  // open: cin, cout
  Multiplier #(.width(16)) multiplier_10 (.a(subtractor_3_out), .b(16'h5), .out(multiplier_10_out));  // open: cin, cout
  Multiplexer #(.width(16)) multiplexer_6 (
    .in0(multiplier_1_out), .in1(negator_2_out), .out(multiplexer_6_out), .sel(comparator_1_lt));  // open: en
  Negator #(.width(16)) negator_2 (.in(multiplier_1_out), .out(negator_2_out));
  Comparator #(.width(16)) comparator_1 (.a(multiplier_1_out), .b({16{1'b0}}), .lt(comparator_1_lt));  // open: gt, eq
  Multiplexer #(.width(16)) multiplexer_7 (
    .in0(multiplier_10_out), .in1(negator_3_out), .out(multiplexer_7_out), .sel(comparator_2_lt));  // open: en
  Negator #(.width(16)) negator_3 (.in(multiplier_10_out), .out(negator_3_out));
  Comparator #(.width(16)) comparator_2 (.a(multiplier_10_out), .b({16{1'b0}}), .lt(comparator_2_lt));  // open: gt, eq
  Divider #(.width(16)) divider_2 (.a(multiplier_2_out), .b(16'h64), .out(divider_2_out));  // open: upper, rem
  Divider #(.width(16)) divider_3 (.a(multiplier_3_out), .b(16'h64), .out(divider_3_out));  // open: upper, rem
  Divider #(.width(16)) divider_4 (.a(divider_1_out), .b(16'h1), .out(divider_4_out));  // open: upper, rem
  Divider #(.width(16)) divider_5 (.a(multiplier_4_out), .b(16'ha), .out(divider_5_out));  // open: upper, rem
  Divider #(.width(16)) divider_6 (.a(multiplier_5_out), .b(16'h64), .out(divider_6_out));  // open: upper, rem
  Divider #(.width(16)) divider_7 (.a(multiplier_6_out), .b(16'h64), .out(divider_7_out));  // open: upper, rem
  Divider #(.width(16)) divider_8 (.a(multiplier_7_out), .b(16'h64), .out(divider_8_out));  // open: upper, rem
  Divider #(.width(16)) divider_9 (.a(multiplier_8_out), .b(16'ha), .out(divider_9_out));  // open: upper, rem
  Divider #(.width(16)) divider_10 (.a(multiplier_9_out), .b(16'h64), .out(divider_10_out));  // open: upper, rem
  Divider #(.width(16)) divider_11 (.a(multiplexer_6_out), .b(16'h64), .out(divider_11_out));  // open: upper, rem
  Negator #(.width(16)) negator_4 (.in(divider_11_out), .out(negator_4_out));
  Divider #(.width(16)) divider_12 (.a(multiplexer_7_out), .b(16'h9), .out(divider_12_out));  // open: upper, rem
  Multiplexer #(.width(16)) multiplexer_8 (
    .in0(divider_11_out), .in1(negator_4_out), .out(multiplexer_8_out), .sel(comparator_1_lt));  // open: en
  Multiplexer #(.width(16)) multiplexer_9 (
    .in0(divider_12_out), .in1(negator_5_out), .out(multiplexer_9_out), .sel(comparator_2_lt));  // open: en
  Negator #(.width(16)) negator_5 (.in(divider_12_out), .out(negator_5_out));
  assign input11 = demultiplexer_4_out0 | divider_8_out | divider_9_out | divider_10_out;  // OR_Gate or_1, 16 bits wide
  Multiplexer #(.select(2), .width(16)) multiplexer_10 (
    .in0(demultiplexer_5_out0), .in1(multiplexer_8_out), .in2(subtractor_2_out), .in3(multiplexer_9_out),
    .out(multiplexer_10_out), .sel(in_4));  // open: en
  assign input31 = demultiplexer_2_out0 | divider_2_out | divider_3_out | divider_4_out;  // OR_Gate or_2, 16 bits wide
  assign input41 = demultiplexer_3_out0 | divider_5_out | divider_6_out | divider_7_out;  // OR_Gate or_3, 16 bits wide
  Multiplier #(.width(16)) multiplier_11 (.a(input11), .b(16'h27), .out(multiplier_11_out));  // open: cin, cout
  Multiplier #(.width(16)) multiplier_12 (.a(input11), .b(16'h21), .out(multiplier_12_out));  // open: cin, cout
  Multiplier #(.width(16)) multiplier_13 (.a(input11), .b(16'hb), .out(multiplier_13_out));  // open: cin, cout
  Multiplier #(.width(16)) multiplier_14 (.a(input31), .b(16'h16), .out(multiplier_14_out));  // open: cin, cout
  Multiplier #(.width(16)) multiplier_15 (.a(input31), .b(16'h161), .out(multiplier_15_out));  // open: cin, cout
  Multiplier #(.width(16)) multiplier_16 (.a(input31), .b(16'ha), .out(multiplier_16_out));  // open: cin, cout
  Multiplier #(.width(16)) multiplier_17 (.a(input41), .b(16'h1a), .out(multiplier_17_out));  // open: cin, cout
  Multiplier #(.width(16)) multiplier_18 (.a(input41), .b(16'h2a), .out(multiplier_18_out));  // open: cin, cout
  Multiplier #(.width(16)) multiplier_19 (.a(input41), .b(16'h15), .out(multiplier_19_out));  // open: cin, cout
  Multiplier #(.width(16)) multiplier_20 (
    .a(multiplexer_10_out), .b(16'h9), .out(multiplier_20_out));  // open: cin, cout
  Multiplier #(.width(16)) multiplier_21 (
    .a(multiplexer_10_out), .b(16'h9), .out(multiplier_21_out));  // open: cin, cout
  Divider #(.width(16)) divider_13 (.a(multiplier_11_out), .b(16'h1), .out(input12));  // open: upper, rem
  Divider #(.width(16)) divider_14 (.a(multiplier_12_out), .b(16'ha), .out(input13));  // open: upper, rem
  Divider #(.width(16)) divider_15 (.a(multiplier_13_out), .b(16'ha), .out(input14));  // open: upper, rem
  Negator #(.width(16)) negator_6 (.in(multiplier_20_out), .out(negator_6_out));
  Comparator #(.width(16)) comparator_3 (.a(multiplier_20_out), .b({16{1'b0}}), .lt(comparator_3_lt));  // open: gt, eq
  Negator #(.width(16)) negator_7 (.in(multiplier_21_out), .out(negator_7_out));
  Comparator #(.width(16)) comparator_4 (.a(multiplier_21_out), .b({16{1'b0}}), .lt(comparator_4_lt));  // open: gt, eq
  Divider #(.width(16)) divider_16 (.a(multiplier_14_out), .b(16'ha), .out(input32));  // open: upper, rem
  Divider #(.width(16)) divider_17 (.a(multiplier_15_out), .b(16'ha), .out(input33));  // open: upper, rem
  Divider #(.width(16)) divider_18 (.a(multiplier_16_out), .b(16'h1), .out(input34));  // open: upper, rem
  Divider #(.width(16)) divider_19 (.a(multiplier_17_out), .b(16'h64), .out(input42));  // open: upper, rem
  Divider #(.width(16)) divider_20 (.a(multiplier_18_out), .b(16'ha), .out(input43));  // open: upper, rem
  Divider #(.width(16)) divider_21 (.a(multiplier_19_out), .b(16'ha), .out(input44));  // open: upper, rem
  Multiplexer #(.width(16)) multiplexer_11 (
    .in0(multiplier_20_out), .in1(negator_6_out), .out(multiplexer_11_out), .sel(comparator_3_lt));  // open: en
  Divider #(.width(16)) divider_22 (.a(multiplexer_11_out), .b(16'h5), .out(divider_22_out));  // open: upper, rem
  Multiplexer #(.width(16)) multiplexer_12 (
    .in0(multiplier_21_out), .in1(negator_7_out), .out(multiplexer_12_out), .sel(comparator_4_lt));  // open: en
  Divider #(.width(16)) divider_23 (.a(multiplexer_12_out), .b(16'h5), .out(divider_23_out));  // open: upper, rem
  Negator #(.width(16)) negator_8 (.in(divider_22_out), .out(negator_8_out));
  Negator #(.width(16)) negator_9 (.in(divider_23_out), .out(negator_9_out));
  Multiplexer #(.width(16)) multiplexer_13 (
    .in0(divider_22_out), .in1(negator_8_out), .out(multiplexer_13_out), .sel(comparator_3_lt));  // open: en
  Multiplexer #(.width(16)) multiplexer_14 (
    .in0(divider_23_out), .in1(negator_9_out), .out(multiplexer_14_out), .sel(comparator_4_lt));  // open: en
  Adder #(.width(16)) adder_1 (.a(multiplexer_13_out), .b(16'h20), .out(adder_1_out));  // open: cin, cout
  Adder #(.width(16)) adder_2 (.a(multiplexer_10_out), .b(16'h111), .out(adder_2_out));  // open: cin, cout
  Adder #(.width(16)) adder_3 (.a(multiplexer_14_out), .b(16'h1eb), .out(adder_3_out));  // open: cin, cout
  Comparator #(.width(16)) comparator_5 (.a(multiplexer_10_out), .b({16{1'b0}}), .lt(out_9));  // open: gt, eq
  Comparator #(.width(16)) comparator_6 (.a(adder_1_out), .b({16{1'b0}}), .lt(out_10));  // open: gt, eq
  Comparator #(.width(16)) comparator_7 (.a(adder_2_out), .b({16{1'b0}}), .lt(out_11));  // open: gt, eq
  Negator #(.width(16)) negator_10 (.in(adder_3_out), .out(negator_10_out));
  Comparator #(.width(16)) comparator_8 (.a(adder_3_out), .b({16{1'b0}}), .lt(out_12));  // open: gt, eq
  Multiplexer #(.width(16)) multiplexer_15 (
    .in0(multiplexer_10_out), .in1(negator_11_out), .out(input21), .sel(out_9));  // open: en
  Negator #(.width(16)) negator_11 (.in(multiplexer_10_out), .out(negator_11_out));
  Multiplexer #(.width(16)) multiplexer_16 (
    .in0(adder_1_out), .in1(negator_12_out), .out(input22), .sel(out_10));  // open: en
  Negator #(.width(16)) negator_12 (.in(adder_1_out), .out(negator_12_out));
  Multiplexer #(.width(16)) multiplexer_17 (
    .in0(adder_2_out), .in1(negator_13_out), .out(input23), .sel(out_11));  // open: en
  Negator #(.width(16)) negator_13 (.in(adder_2_out), .out(negator_13_out));
  Multiplexer #(.width(16)) multiplexer_18 (
    .in0(adder_3_out), .in1(negator_10_out), .out(input24), .sel(out_12));  // open: en

  assign Fahrenheite = Celsius;
  assign Gallons = Cups;
  assign Inch = Foot;
  assign Kelvin = Celsius;
  assign Kg = Force;
  assign Liter = Cups;
  assign Meters = Foot;
  assign Ounce = Force;
  assign out_20 = Celsius;
  assign Pints = Cups;
  assign Pound = Force;
  assign Yard = Foot;

  // Other names for the same wires on the sheet: dimInput[1:0] = in_1; maininput[10:0] = in_2; mux[1:0] = in_4;
  //   neg21 = out_9; neg22 = out_10; neg23 = out_11; neg24 = out_12; negativetemperature = in_3;
  //   output1[15:0] = out_5; output2[15:0] = out_6; output3[15:0] = out_7; output4[15:0] = out_8; segment1 = Foot;
  //   segment2 = Celsius; segment3 = Force; segment4 = Cups

  // Notes on the sheet:
  //   keyboard
  //   OTHER
  //   Bit extender
  //   I/P
  //   00
  //   01
  //   10
  //   11
  //   I/P
  //   Meters
  //   00
  //   Inch
  //   01
  //   Foot
  //   10
  //   11
  //   Yard
  //   Dimension input:
  //   Dimension
  //   Length
  //   Temperature
  //   Weight
  //   Volume of liquid
  //   Length
  //   Temperature
  //   Celsius
  //   Fahrenheite
  //   Kelvin
  //   Rankine
  //   INPUT
  //   Value Input in:
  //   Weight
  //   Kg
  //   Ounce
  //   Pound
  //   Force
  //   Input value:
  //   Volume of liquid
  //   Liter
  //   Gallons
  //   Cups
  //   Pints
  //   Length
  //   temperature
  //   mass
  //   volume
  //   kg TO kg
  //   pound TO kg
  //   ounce TO kg
  //   Force to kg
  //   liter TO liter
  //   gallon TO liter
  //   cups TO liter
  //   pints TO liter
  //   CONVERSION CIRCUIT
  //   Meter TO Meter
  //   Inch TO Meter
  //   Foot TO Meter
  //   Yard TO Meter
  //   celcius TO celcius
  //   kelvin TO celcius
  //   rankine TO celcius
  //   ------------------------------------------------------------------------------------------------------------------------------------------------------------------------------------------------------------------------------------------------------------------------------------------------------------
  //   fahrenheit TO celcius
  //   ------------------------------------------------------------------------------------------------------------------------------------------------------------------------------------------------------------------------------------------------------------------------------------------------------------
  //   OUTPUT
  //   Meter
  //   Inch
  //   foot
  //   kg
  //   pound
  //   ounce
  //   force
  //   liter
  //   gallon
  //   cups
  //   pints
  //   Yard
  //   celcius
  //   fahrenheit
  //   kelvin
  //   rankine
  //   Rankine
endmodule
